// Logisim project CPU.circ as structural Verilog: 1 circuit, main circuit main
module main (
  input  RST
);

  wire CLK, decoder_1_out1, decoder_1_out2, decoder_1_out3, decoder_1_out4, decoder_2_out8, decoder_2_out9,
       decoder_2_out14, decoder_2_out15, decoder_2_out16, decoder_2_out17, decoder_2_out18, decoder_2_out19,
       decoder_2_out20, decoder_2_out21, decoder_2_out22, decoder_2_out23, decoder_2_out24, decoder_2_out25,
       decoder_2_out26, decoder_2_out27, j_k_ff_1_q, j_k_ff_2_q, PC_INC, RAM_WRITE, ST0, ST1, ST2, ST3;
  wire [4:0] bit_extender_1_out, REG_ADDR, REGX;
  wire [5:0] OPCODE;
  wire [15:0] A_q, adder_1_out, B_q, C_q, D_q, IMM16, JMP, multiplexer_1_out, PC, RAM_ADDR, RAM_IN, RAM_OUT,
       REG_IN, REG_OUT;
  wire [31:0] rom_1_data;

  Clock clock_1 (.out(CLK));
  Adder #(.width(16)) adder_1 (.a(PC), .b(16'h1), .out(adder_1_out));  // open: cin, cout
  // Probe on PC
  Multiplexer #(.width(16)) multiplexer_1 (.in0(JMP), .in1(adder_1_out), .out(multiplexer_1_out), .sel(PC_INC));
  ROM #(.addrWidth(16), .dataWidth(32)) rom_1 (.addr(PC), .data(rom_1_data));
  RAM #(.addrWidth(16), .dataWidth(16)) ram_1 (
    .addr(RAM_ADDR), .we(RAM_WRITE), .oe(CLK), .din(RAM_IN), .dout(RAM_OUT));  // open: clk
  Register #(.width(16)) register_1 (.D(multiplexer_1_out), .en(PC_INC), .clk(CLK), .Q(PC), .clr(RST));
  // Probe on rom_1_data
  Decoder #(.select(5)) decoder_1 (
    .out1(decoder_1_out1), .out2(decoder_1_out2), .out3(decoder_1_out3), .out4(decoder_1_out4),
    .sel(REG_ADDR), .en(1'b0));  // open: out0, out5, out6, out7, out8, out9, out10, out11, out12, out13, out14, out15, out16, out17, out18, out19, out20, out21, out22, out23, out24, out25, out26, out27, out28, out29, out30, out31
  Register #(.width(32)) register_2 (
    .D(rom_1_data), .en(ST0), .clk(CLK), .Q({OPCODE, REGX, REG_ADDR, IMM16}), .clr(RST));
  Decoder #(.select(5)) decoder_2 (
    .out0(PC_INC), .out8(decoder_2_out8), .out9(decoder_2_out9), .out14(decoder_2_out14),
    .out15(decoder_2_out15), .out16(decoder_2_out16), .out17(decoder_2_out17), .out18(decoder_2_out18),
    .out19(decoder_2_out19), .out20(decoder_2_out20), .out21(decoder_2_out21), .out22(decoder_2_out22),
    .out23(decoder_2_out23), .out24(decoder_2_out24), .out25(decoder_2_out25), .out26(decoder_2_out26),
    .out27(decoder_2_out27), .sel(bit_extender_1_out), .en(1'b1));  // open: out1, out2, out3, out4, out5, out6, out7, out10, out11, out12, out13, out28, out29, out30, out31
  Bit_Extender #(.in_width(6), .out_width(5)) bit_extender_1 (.in(OPCODE), .out(bit_extender_1_out));
  Register #(.width(16)) A (.D(REG_IN), .en(decoder_1_out1), .clk(CLK), .Q(A_q), .clr(RST));
  Register #(.width(16)) B (.D(REG_IN), .en(decoder_1_out2), .clk(CLK), .Q(B_q), .clr(RST));
  Register #(.width(16)) C (.D(REG_IN), .en(decoder_1_out3), .clk(CLK), .Q(C_q), .clr(RST));
  Register #(.width(16)) D (.D(REG_IN), .en(decoder_1_out4), .clk(CLK), .Q(D_q), .clr(RST));
  // Buffer ADD has open pins: in=decoder_2_out8, out=open
  // Buffer SUB has open pins: in=decoder_2_out9, out=open
  // Buffer SHR has open pins: in=decoder_2_out14, out=open
  // Buffer SHL has open pins: in=decoder_2_out15, out=open
  // Buffer ROTR has open pins: in=decoder_2_out16, out=open
  // Buffer ROTL has open pins: in=decoder_2_out17, out=open
  // Buffer ADDI has open pins: in=decoder_2_out18, out=open
  // Buffer SUBI has open pins: in=decoder_2_out19, out=open
  // Buffer LOAD has open pins: in=decoder_2_out20, out=open
  // Buffer STORE has open pins: in=decoder_2_out21, out=open
  // Buffer INP has open pins: in=decoder_2_out22, out=open
  // Buffer OUTP has open pins: in=decoder_2_out23, out=open
  // Buffer JUMP has open pins: in=decoder_2_out24, out=open
  // Buffer JZ has open pins: in=decoder_2_out25, out=open
  // Buffer JN has open pins: in=decoder_2_out26, out=open
  // Buffer JC has open pins: in=decoder_2_out27, out=open
  Multiplexer #(.select(5), .width(16)) multiplexer_2 (
    .in1(A_q), .in2(B_q), .in3(C_q), .in4(D_q), .out(REG_OUT), .sel(REG_ADDR));  // open: in0, in5, in6, in7, in8, in9, in10, in11, in12, in13, in14, in15, in16, in17, in18, in19, in20, in21, in22, in23, in24, in25, in26, in27, in28, in29, in30, in31
  and and_1 (ST1, j_k_ff_1_q, j_k_ff_2_q);
  J_K_Flip_Flop j_k_ff_1 (.J(1'b1), .K(1'b1), .clk(CLK), .Q(j_k_ff_1_q), .reset(RST));  // open: Qn, preset
  and and_2 (ST2, ~j_k_ff_1_q, j_k_ff_2_q);  // AND_Gate
  and and_3 (ST3, j_k_ff_1_q, ~j_k_ff_2_q);  // AND_Gate
  J_K_Flip_Flop j_k_ff_2 (.J(1'b1), .K(1'b1), .clk(j_k_ff_1_q), .Q(j_k_ff_2_q), .reset(RST));  // open: Qn, preset
  and and_4 (ST0, ~ST1, ~ST2, ~ST3);  // AND_Gate
  ALU alu_1 (.A(REG_OUT), .B(IMM16));  // open: CIN, SEL, OVER, SIGN, HOUT, OUTP, COUT, LT, GT, EQ, ZERO

  // Other names for the same wires on the sheet: REGY[4:0] = REG_ADDR; PC_SET = PC_INC

  // Notes on the sheet:
  //   contents of rom_1 (hex, n*v repeats v):
  //   1
  //   NOP
endmodule
